# Fritzing sketch piirilevy (saved by Fritzing 0.9.2b)
perfboards: 1

parts:
  Part1 = Arduino Nano (Rev3.0)
  C1 = Electrolytic Capacitor [capacitance=1µF package="100 mil [THT, electrolytic]"]
  J1 = female pin header, 6 pins [form="♀ (female)"]
  J2 = double row female pin header, 4 pins [form="♀ (female)"]
  R1 = Resistor [tolerance=±5% resistance=220 package=THT]
  LED1 = LED - 5mm [color="Green (555nm)" package="5 mm [THT]"]
  R2 = Resistor [tolerance=±5% resistance=220 package=THT]
  LED2 = LED - 5mm [color="Blue (430nm)" package="5 mm [THT]"]

nets:
  N1: Part1.GND, C1.-, J1.pin4, J2.pin4, LED1.cathode, LED2.cathode
  N2: Part1.D4, R2.Pin_0
  N3: Part1.D5, J1.pin6
  N4: Part1.D6, J1.pin5
  N5: Part1.D9, J1.pin2
  N6: Part1.D10, J1.pin1
  N7: Part1.VIN, C1.+, J1.pin3
  N8: Part1.5V, J2.pin1, R1.Pin_0
  N9: Part1.A5, J2.pin3
  N10: Part1.A4, J2.pin2
  N11: R1.Pin_1, LED1.anode
  N12: R2.Pin_1, LED2.anode
